// Logisim project projv3.circ as structural Verilog: 9 circuits, main circuit main
// NPC
module main (
);

  wire Clk, EXBEQ, EXBNE, EXMemRd, EXRegWr, ExtOp, ImmSel, Jal, JalIn, Jump, Kill1, Kill2, MEMRd, MemRd_t,
       MEMRegWr, MEMWBdata, MEMWr, MemWr_t, not_1_out, not_2_out, not_3_out, not_4_out, not_5_out, not_6_out,
       or_1_out, or_2_out, register_1_q, register_3_q, RegWr, REV, Stall, WBdata, WBRegWr, ZeroFlag;
  wire [1:0] AluSrc, EXAluSrc, F, FwA, FwB, PCSrc, RegDst;
  wire [2:0] multiplexer_4_out, Rd2Out, Rd3Out, Rd4Out, RdMxOUT, Rs, Rt;
  wire [3:0] AluOp, EXAluOp;
  wire [4:0] Op;
  wire [8:6] INST_q;
  wire [13:0] EX_q;
  wire [14:0] multiplexer_8_out;
  wire [15:0] A_q, adder_1_out, adder_2_out, B_q, BTA, D_q, Data_Memory_dout, ext_1_immout, FwAlu, FwMem,
       FwWB, IMM_q, Instruction_Memory_data, JalValIn, JalValPipe, multiplexer_1_out, multiplexer_2_out,
       multiplexer_5_out, multiplexer_6_out, multiplexer_7_out, multiplexer_9_out, PC, PcAdjust, R_q,
       regfile_1_busa, regfile_1_busb, register_2_q, register_4_q, shifter_1_out;

  Clock u_clk (.out(Clk));
  Multiplexer #(.select(2), .width(16)) multiplexer_1 (
    .in0(adder_1_out), .in1(ext_1_immout), .in2(BTA), .in3(multiplexer_6_out), .out(multiplexer_1_out),
    .sel(PCSrc));
  not not_1 (not_1_out, Stall);
  PcCtrl2 pcctrl2_1 (
    .Op(Op), .Zero(ZeroFlag), .Func(F), .Jump(or_1_out), .EX_BEQ(EXBEQ), .EX_BNE(EXBNE), .PCSrc(PCSrc),
    .Kill1(Kill1), .Kill2(Kill2));
  or or_1 (or_1_out, Jal, Jump);
  ROM #(.addrWidth(16), .dataWidth(16)) Instruction_Memory (.addr(PcAdjust), .data(Instruction_Memory_data));
  Register #(.width(16)) u_PC (.D(multiplexer_1_out), .en(not_1_out), .Q(PcAdjust), .clk(Clk));  // open: clr
  Subtractor #(.width(16)) subtractor_1 (.a(PcAdjust), .b(16'h1), .out(PC));  // open: bin, bout
  Adder #(.width(16)) adder_1 (.a(16'h1), .b(PcAdjust), .out(adder_1_out));  // open: cin, cout
  CtrlUnit ctrlunit_1 (
    .Op(Op), .Jump(Jump), .RegDst(RegDst), .ExtOp(ExtOp), .ImmSel(ImmSel), .RegWr(RegWr), .AluSrc(AluSrc),
    .MemRd(MemRd_t), .MemWr(MemWr_t), .WBdata(WBdata), .jal(Jal), .REV(REV));
  Register #(.width(16)) NPC (.D(adder_1_out), .Q(JalValPipe), .clk(Clk));  // open: en, clr
  Multiplexer #(.width(16)) multiplexer_2 (
    .in0(Instruction_Memory_data), .in1({16{1'b0}}), .out(multiplexer_2_out), .sel(Kill1));
  Register #(.width(16)) INST (
    .D(multiplexer_2_out), .en(not_2_out), .Q({Op, F, INST_q, Rs, Rt}), .clk(Clk));  // open: clr
  not not_2 (not_2_out, Stall);
  HazardCtrl hazardctrl_1 (
    .Rs(Rs), .Rd4Out(Rd4Out), .WBRegWr(WBRegWr), .Rd3Out(Rd3Out), .MEMRegWr(MEMRegWr), .Rd2Out(Rd2Out),
    .EXRegWr(EXRegWr), .EXMemRd(EXMemRd), .Rt(Rt), .FwA(FwA), .Stall(Stall), .FwB(FwB));
  AluCtrl aluctrl_1 (.f(F), .Op(Op), .AluOp(AluOp));
  Multiplexer #(.select(2), .width(3)) multiplexer_3 (
    .in0(Rt), .in1(INST_q), .in2(3'b001), .in3(3'b111), .out(RdMxOUT), .sel(RegDst));
  Multiplexer #(.width(3)) multiplexer_4 (.in0(Rt), .in1(INST_q), .out(multiplexer_4_out), .sel(REV));
  Multiplexer #(.width(16)) multiplexer_5 (.in0(FwWB), .in1(JalValIn), .out(multiplexer_5_out), .sel(JalIn));
  Ext ext_1 (.Imm5({F, INST_q}), .Imm11({F, INST_q, Rs, Rt}), .ExtOp(ExtOp), .ImmSel(ImmSel), .ImmOut(ext_1_immout));
  RegFile regfile_1 (
    .RA(Rs), .RB(multiplexer_4_out), .BusW(multiplexer_5_out), .RW(Rd4Out), .RegWrite(WBRegWr), .clk(Clk),
    .BusA(regfile_1_busa), .BusB(regfile_1_busb));
  or or_2 (or_2_out, Kill2, Stall);
  Adder #(.width(16)) adder_2 (.a(PC), .b(ext_1_immout), .out(adder_2_out));  // open: cin, cout
  Multiplexer #(.select(2), .width(16)) multiplexer_6 (
    .in0(regfile_1_busa), .in1(FwWB), .in2(FwMem), .in3(FwAlu), .out(multiplexer_6_out), .sel(FwA));
  Multiplexer #(.select(2), .width(16)) multiplexer_7 (
    .in0(regfile_1_busb), .in1(FwWB), .in2(FwMem), .in3(FwAlu), .out(multiplexer_7_out), .sel(FwB));
  not not_3 (not_3_out, Stall);
  Multiplexer #(.width(15)) multiplexer_8 (
    .in0({RegWr, WBdata, MemWr_t, MemRd_t, AluSrc, AluOp, Op}), .in1({15{1'b0}}), .out(multiplexer_8_out),
    .sel(or_2_out));
  Register #(.width(16)) u_BTA (.D(adder_2_out), .en(not_3_out), .Q(BTA), .clk(Clk));  // open: clr
  Register #(.width(16)) IMM (.D(ext_1_immout), .en(not_3_out), .Q(IMM_q), .clk(Clk));  // open: clr
  Register #(.width(16)) A (.D(multiplexer_6_out), .en(not_3_out), .Q(A_q), .clk(Clk));  // open: clr
  Register #(.width(16)) B (.D(multiplexer_7_out), .en(not_3_out), .Q(B_q), .clk(Clk));  // open: clr
  Register #(.width(3)) Rd2 (.D(RdMxOUT), .en(not_3_out), .Q(Rd2Out), .clk(Clk));  // open: clr
  Register #(.width(1)) register_1 (.D(Jal), .en(not_3_out), .Q(register_1_q), .clk(Clk));  // open: clr
  Register #(.width(16)) register_2 (.D(JalValPipe), .en(not_3_out), .Q(register_2_q), .clk(Clk));  // open: clr
  Register #(.width(15)) EX (
    .D(multiplexer_8_out), .Q({EXRegWr, EX_q[13:12], EXMemRd, EXAluSrc, EXAluOp, EX_q[4:0]}), .clk(Clk));  // open: en, clr
  Shifter #(.width(16)) shifter_1 (.in(IMM_q), .\dist (4'b0101), .out(shifter_1_out));
  Multiplexer #(.select(2), .width(16)) multiplexer_9 (
    .in0(B_q), .in1(shifter_1_out), .in2(IMM_q), .in3({16{1'b0}}), .out(multiplexer_9_out), .sel(EXAluSrc));
  not not_4 (not_4_out, EX_q[0]);
  and and_1 (EXBEQ, not_4_out, EX_q[1], EX_q[2], EX_q[3], not_5_out);
  not not_5 (not_5_out, EX_q[4]);
  and and_2 (EXBNE, EX_q[0], EX_q[1], EX_q[2], EX_q[3], not_6_out);
  not not_6 (not_6_out, EX_q[4]);
  ALU alu_1 (.A(A_q), .B(multiplexer_9_out), .AluOp(EXAluOp), .ALUResult(FwAlu), .Zero(ZeroFlag));
  Register #(.width(16)) R (.D(FwAlu), .Q(R_q), .clk(Clk));  // open: en, clr
  Register #(.width(16)) D (.D(B_q), .Q(D_q), .clk(Clk));  // open: en, clr
  Register #(.width(3)) Rd3 (.D(Rd2Out), .Q(Rd3Out), .clk(Clk));  // open: en, clr
  Register #(.width(1)) register_3 (.D(register_1_q), .Q(register_3_q), .clk(Clk));  // open: en, clr
  Register #(.width(16)) register_4 (.D(register_2_q), .Q(register_4_q), .clk(Clk));  // open: en, clr
  Register #(.width(4)) MEM (
    .D({EXRegWr, EX_q[13:12], EXMemRd}), .Q({MEMRegWr, MEMWBdata, MEMWr, MEMRd}), .clk(Clk));  // open: en, clr
  RAM #(.addrWidth(16), .asyncread("true"), .dataWidth(16)) Data_Memory (
    .addr(R_q), .we(MEMWr), .oe(MEMRd), .clk(Clk), .din(D_q), .dout(Data_Memory_dout));
  Multiplexer #(.width(16)) multiplexer_10 (.in0(R_q), .in1(Data_Memory_dout), .out(FwMem), .sel(MEMWBdata));
  Register #(.width(16)) Data (.D(FwMem), .Q(FwWB), .clk(Clk));  // open: en, clr
  Register #(.width(3)) Rd4 (.D(Rd3Out), .Q(Rd4Out), .clk(Clk));  // open: en, clr
  Register #(.width(1)) register_5 (.D(register_3_q), .Q(JalIn), .clk(Clk));  // open: en, clr
  Register #(.width(16)) register_6 (.D(register_4_q), .Q(JalValIn), .clk(Clk));  // open: en, clr
  Register #(.width(1)) WB (.D(MEMRegWr), .Q(WBRegWr), .clk(Clk));  // open: en, clr

  // Other names for the same wires on the sheet: JalSigPipe = Jal; RdIN[2:0] = Rd4Out

  // Notes on the sheet:
  //   contents of Instruction_Memory (hex, n*v repeats v):
  //   4281 4742 4643 4644 4085 104d 1295 14dd 1725 6801 6842 6883 68c4 40 80 c0 100 6001 6042 6083 60c4
  //   881a 94b daa 5337 8019 551 7105 c4a c8a c4a 55a 7105 c93 cd3 c93 563 7105 cdc d1c cdc 551 7105 c4a
  //   c8a c4a 55a 7105 c93 cd3 c93 551 7105 c4a c8a c4a 1e38
endmodule

module ALU (
  input  [15:0] A,
  input  [15:0] B,
  input  [3:0] AluOp,
  output [15:0] ALUResult,
  output Zero
);

  wire comparator_1_lt, comparator_2_lt;
  wire [15:0] adder_1_out, and_1_out, bit_extender_1_out, bit_extender_2_out, not_1_out, or_1_out,
       shifter_1_out, shifter_2_out, shifter_3_out, shifter_4_out, subtractor_1_out, xor_1_out;

  Shifter #(.width(16)) shifter_1 (.in(A), .\dist (B[3:0]), .out(shifter_1_out));
  Shifter #(.shift("lr"), .width(16)) shifter_2 (.in(A), .\dist (B[3:0]), .out(shifter_2_out));
  Shifter #(.shift("ar"), .width(16)) shifter_3 (.in(A), .\dist (B[3:0]), .out(shifter_3_out));
  Shifter #(.shift("rr"), .width(16)) shifter_4 (.in(A), .\dist (B[3:0]), .out(shifter_4_out));
  Adder #(.width(16)) adder_1 (.a(A), .b(B), .out(adder_1_out));  // open: cin, cout
  Subtractor #(.width(16)) subtractor_1 (.a(A), .b(B), .out(subtractor_1_out));  // open: bin, bout
  Comparator #(.width(16)) comparator_1 (.a(A), .b(B), .lt(comparator_1_lt));  // open: gt, eq
  Comparator #(.mode("unsigned"), .width(16)) comparator_2 (.a(A), .b(B), .lt(comparator_2_lt));  // open: gt, eq
  assign and_1_out = A & B;  // AND_Gate and_1, 16 bits wide
  assign or_1_out = A | B;  // OR_Gate or_1, 16 bits wide
  assign not_1_out = ~or_1_out;  // NOT_Gate not_1, 16 bits wide
  assign xor_1_out = A ^ B;  // XOR_Gate xor_1, 16 bits wide
  assign bit_extender_1_out = {{15{1'b0}}, comparator_1_lt};  // Bit_Extender bit_extender_1
  assign bit_extender_2_out = {{15{1'b0}}, comparator_2_lt};  // Bit_Extender bit_extender_2
  Multiplexer #(.select(4), .width(16)) multiplexer_1 (
    .in0(adder_1_out), .in1(subtractor_1_out), .in2(bit_extender_1_out), .in3(bit_extender_2_out),
    .in4(and_1_out), .in5(or_1_out), .in6(xor_1_out), .in7(not_1_out), .in8(shifter_1_out),
    .in9(shifter_2_out), .in10(shifter_3_out), .in11(shifter_4_out),
    .in12({B[15:8], A[0], A[1], A[2], A[3], A[4], A[5], A[6], A[7]}),
    .in13({B[15:8], A[8], A[9], A[10], A[11], A[12], A[13], A[14], A[15]}),
    .in14({A[0], A[1], A[2], A[3], A[4], A[5], A[6], A[7], A[8], A[9], A[10], A[11], A[12], A[13], A[14], A[15]}),
    .in15(B), .out(ALUResult), .sel(AluOp));
  Comparator #(.mode("unsigned"), .width(16)) comparator_3 (.a(ALUResult), .b({16{1'b0}}), .eq(Zero));  // open: gt, lt
endmodule

module CtrlUnit (
  input  [4:0] Op,
  output Jump,
  output [1:0] RegDst,
  output ExtOp,
  output ImmSel,
  output RegWr,
  output [1:0] AluSrc,
  output MemRd,
  output MemWr,
  output WBdata,
  output jal,
  output REV
);

  wire and_2_out, and_3_out, and_4_out, and_5_out, and_6_out, and_7_out, and_8_out, and_9_out, and_10_out,
       and_11_out, and_12_out, and_13_out, and_14_out, and_15_out, not_1_out, not_2_out, not_3_out,
       not_4_out, not_5_out;

  not not_1 (not_1_out, Op[4]);
  not not_2 (not_2_out, Op[3]);
  not not_3 (not_3_out, Op[2]);
  not not_4 (not_4_out, Op[1]);
  not not_5 (not_5_out, Op[0]);
  and and_1 (Jump, not_5_out, not_4_out, not_3_out, not_2_out, Op[4]);
  and and_2 (and_2_out, not_2_out, Op[2]);
  and and_3 (and_3_out, not_1_out, not_2_out);
  and and_4 (and_4_out, not_2_out, not_3_out, not_4_out, Op[0]);
  and and_5 (and_5_out, not_1_out, not_2_out);
  and and_6 (and_6_out, not_1_out, not_4_out, not_5_out);
  and and_7 (and_7_out, not_1_out, Op[2]);
  and and_8 (and_8_out, not_2_out, Op[1]);
  and and_9 (and_9_out, not_2_out, Op[2]);
  and and_10 (and_10_out, not_1_out, not_4_out, not_5_out);
  and and_11 (and_11_out, not_1_out, not_3_out);
  and and_12 (and_12_out, not_2_out, not_3_out, Op[0]);
  and and_13 (and_13_out, Op[4], Op[1]);
  and and_14 (and_14_out, Op[3], not_3_out);
  and and_15 (and_15_out, Op[2], not_4_out);
  and and_16 (AluSrc[0], Op[4], Op[1]);
  and and_17 (MemRd, Op[2], not_4_out, not_5_out);
  and and_18 (MemWr, Op[2], not_4_out, Op[0]);
  and and_19 (WBdata, Op[2], not_4_out, not_5_out);
  and and_20 (jal, Op[4], not_2_out, not_3_out, not_4_out, Op[0]);
  and and_21 (REV, not_1_out, not_2_out, not_3_out, Op[1], Op[0]);
  or or_1 (RegDst[1], and_2_out, Op[4]);
  or or_2 (RegDst[0], and_3_out, and_4_out);
  or or_3 (ExtOp, and_5_out, and_6_out, and_7_out, and_8_out, and_9_out);
  or or_4 (RegWr, and_10_out, and_11_out, and_12_out, and_13_out);
  or or_5 (AluSrc[1], and_14_out, and_15_out);

  assign ImmSel = Op[4];
endmodule

module AluCtrl (
  input  [1:0] f,
  input  [4:0] Op,
  output [3:0] AluOp
);

  Multiplexer #(.select(5), .width(4)) multiplexer_1 (
    .in0({Op[1:0], f}), .in1({Op[1:0], f}), .in2({Op[1:0], f}), .in3({Op[1:0], f}), .in4(4'b0000),
    .in5(4'b0101), .in6(4'b0000), .in7(4'b0000), .in8(4'b0000), .in9(4'b0100), .in10(4'b0000),
    .in11(4'b0000), .in12(4'b0000), .in13(4'b0000), .in14(4'b0001), .in15(4'b0001), .in16(4'b0000),
    .in17(4'b1111), .in18(4'b0000), .in19(4'b0000), .in20(4'b0000), .in21(4'b0000), .in22(4'b0000),
    .in23(4'b0000), .in24(4'b0000), .in25(4'b0000), .in26(4'b0000), .in27(4'b0000), .in28(4'b0000),
    .in29(4'b0000), .in30(4'b0000), .in31(4'b1111), .out(AluOp), .sel(Op));
endmodule

module Ext (
  input  [4:0] Imm5,
  input  [10:0] Imm11,
  input  ExtOp,
  input  ImmSel,
  output [15:0] ImmOut
);

  wire [15:0] bit_extender_1_out, bit_extender_2_out, bit_extender_3_out, bit_extender_4_out,
       multiplexer_1_out, multiplexer_2_out;

  assign bit_extender_1_out = {{11{1'b0}}, Imm5};  // Bit_Extender bit_extender_1
  assign bit_extender_2_out = {{11{Imm5[4]}}, Imm5};  // Bit_Extender bit_extender_2
  assign bit_extender_3_out = {{5{1'b0}}, Imm11};  // Bit_Extender bit_extender_3
  assign bit_extender_4_out = {{5{Imm11[10]}}, Imm11};  // Bit_Extender bit_extender_4
  Multiplexer #(.width(16)) multiplexer_1 (
    .in0(bit_extender_1_out), .in1(bit_extender_2_out), .out(multiplexer_1_out), .sel(ExtOp));
  Multiplexer #(.width(16)) multiplexer_2 (
    .in0(bit_extender_3_out), .in1(bit_extender_4_out), .out(multiplexer_2_out), .sel(ExtOp));
  Multiplexer #(.width(16)) multiplexer_3 (
    .in0(multiplexer_1_out), .in1(multiplexer_2_out), .out(ImmOut), .sel(ImmSel));
endmodule

module RegFile (
  input  [2:0] RA,
  input  [2:0] RB,
  input  [15:0] BusW,
  input  [2:0] RW,
  input  RegWrite,
  input  clk,
  output [15:0] BusA,
  output [15:0] BusB
);

  wire and_1_out, and_2_out, and_3_out, and_4_out, and_5_out, and_6_out, and_7_out, decoder_1_out1,
       decoder_1_out2, decoder_1_out3, decoder_1_out4, decoder_1_out5, decoder_1_out6, decoder_1_out7,
       decoder_2_out0, decoder_2_out1, decoder_2_out2, decoder_2_out3, decoder_2_out4, decoder_2_out5,
       decoder_2_out6, decoder_2_out7, decoder_3_out0, decoder_3_out1, decoder_3_out2, decoder_3_out3,
       decoder_3_out4, decoder_3_out5, decoder_3_out6, decoder_3_out7;
  wire [15:0] r1, r2, r3, r4, r5, r6, r7;

  Decoder #(.enable("false"), .select(3)) decoder_1 (
    .out1(decoder_1_out1), .out2(decoder_1_out2), .out3(decoder_1_out3), .out4(decoder_1_out4),
    .out5(decoder_1_out5), .out6(decoder_1_out6), .out7(decoder_1_out7), .sel(RW));  // open: out0
  and and_1 (and_1_out, decoder_1_out1, RegWrite);
  and and_2 (and_2_out, decoder_1_out2, RegWrite);
  and and_3 (and_3_out, decoder_1_out3, RegWrite);
  and and_4 (and_4_out, decoder_1_out4, RegWrite);
  and and_5 (and_5_out, decoder_1_out5, RegWrite);
  and and_6 (and_6_out, decoder_1_out6, RegWrite);
  and and_7 (and_7_out, decoder_1_out7, RegWrite);
  Register #(.width(16)) u_R1 (.D(BusW), .en(and_1_out), .Q(r1), .clk(clk));  // open: clr
  Register #(.width(16)) u_R2 (.D(BusW), .en(and_2_out), .Q(r2), .clk(clk));  // open: clr
  Register #(.width(16)) u_R3 (.D(BusW), .en(and_3_out), .Q(r3), .clk(clk));  // open: clr
  Register #(.width(16)) u_R4 (.D(BusW), .en(and_4_out), .Q(r4), .clk(clk));  // open: clr
  Register #(.width(16)) u_R5 (.D(BusW), .en(and_5_out), .Q(r5), .clk(clk));  // open: clr
  Register #(.width(16)) u_R6 (.D(BusW), .en(and_6_out), .Q(r6), .clk(clk));  // open: clr
  Register #(.width(16)) u_R7 (.D(BusW), .en(and_7_out), .Q(r7), .clk(clk));  // open: clr
  Decoder #(.enable("false"), .select(3)) decoder_2 (
    .out0(decoder_2_out0), .out1(decoder_2_out1), .out2(decoder_2_out2), .out3(decoder_2_out3),
    .out4(decoder_2_out4), .out5(decoder_2_out5), .out6(decoder_2_out6), .out7(decoder_2_out7), .sel(RA));
  assign BusA = decoder_2_out0 ? {16{1'b0}} : 16'bz;  // Controlled_Buffer controlled_buffer_1
  assign BusA = decoder_2_out1 ? r1 : 16'bz;  // Controlled_Buffer controlled_buffer_2
  assign BusA = decoder_2_out2 ? r2 : 16'bz;  // Controlled_Buffer controlled_buffer_3
  assign BusA = decoder_2_out3 ? r3 : 16'bz;  // Controlled_Buffer controlled_buffer_4
  assign BusA = decoder_2_out4 ? r4 : 16'bz;  // Controlled_Buffer controlled_buffer_5
  assign BusA = decoder_2_out5 ? r5 : 16'bz;  // Controlled_Buffer controlled_buffer_6
  assign BusA = decoder_2_out6 ? r6 : 16'bz;  // Controlled_Buffer controlled_buffer_7
  assign BusA = decoder_2_out7 ? r7 : 16'bz;  // Controlled_Buffer controlled_buffer_8
  Decoder #(.enable("false"), .select(3)) decoder_3 (
    .out0(decoder_3_out0), .out1(decoder_3_out1), .out2(decoder_3_out2), .out3(decoder_3_out3),
    .out4(decoder_3_out4), .out5(decoder_3_out5), .out6(decoder_3_out6), .out7(decoder_3_out7), .sel(RB));
  assign BusB = decoder_3_out0 ? {16{1'b0}} : 16'bz;  // Controlled_Buffer controlled_buffer_9
  assign BusB = decoder_3_out1 ? r1 : 16'bz;  // Controlled_Buffer controlled_buffer_10
  assign BusB = decoder_3_out2 ? r2 : 16'bz;  // Controlled_Buffer controlled_buffer_11
  assign BusB = decoder_3_out3 ? r3 : 16'bz;  // Controlled_Buffer controlled_buffer_12
  assign BusB = decoder_3_out4 ? r4 : 16'bz;  // Controlled_Buffer controlled_buffer_13
  assign BusB = decoder_3_out5 ? r5 : 16'bz;  // Controlled_Buffer controlled_buffer_14
  assign BusB = decoder_3_out6 ? r6 : 16'bz;  // Controlled_Buffer controlled_buffer_15
  assign BusB = decoder_3_out7 ? r7 : 16'bz;  // Controlled_Buffer controlled_buffer_16
endmodule

module PCCtrl (
  input  Zero,
  input  [4:0] Op,
  input  [1:0] f,
  input  EX_BEQ,
  input  EX_BNE,
  input  Jump,
  output [1:0] PCSrc,
  output [1:0] out_8,
  output Kill1,
  output Kill2
);

  wire and_1_out, and_2_out, and_3_out, and_4_out, and_5_out, and_9_out, and_10_out, J, not_1_out, not_2_out,
       not_3_out, not_4_out, not_5_out, not_6_out, not_7_out, not_8_out, not_9_out, not_10_out, not_11_out,
       not_12_out, not_13_out, not_14_out, not_15_out;

  not not_1 (not_1_out, Zero);
  not not_2 (not_2_out, Op[4]);
  not not_3 (not_3_out, Op[3]);
  not not_4 (not_4_out, Op[2]);
  not not_5 (not_5_out, Op[1]);
  not not_6 (not_6_out, Op[0]);
  and and_1 (and_1_out, Zero, not_2_out, Op[3], Op[2], Op[1], not_6_out);
  and and_2 (and_2_out, not_1_out, not_2_out, Op[3], Op[2], Op[1], Op[0]);
  and and_3 (and_3_out, not_2_out, not_3_out, not_4_out, Op[1], Op[0], f[1], f[0]);
  and and_4 (and_4_out, Op[4], not_3_out, not_4_out, not_5_out);
  and and_5 (and_5_out, not_2_out, not_3_out, not_4_out, Op[1], Op[0], f[1], f[0]);
  or or_1 (PCSrc[1], and_1_out, and_2_out, and_3_out);
  or or_2 (PCSrc[0], and_4_out, and_5_out);
  not not_7 (not_7_out, Op[0]);
  not not_8 (not_8_out, Op[1]);
  not not_9 (not_9_out, Op[2]);
  // AND_Gate and_6 has open pins: in0=not_7_out, in1=not_8_out, in2=not_9_out, in3=not_10_out, in4=Op[4], out=open
  not not_10 (not_10_out, Op[3]);
  not not_11 (not_11_out, Op[0]);
  // AND_Gate and_7 has open pins: in0=not_11_out, in1=Op[1], in2=Op[2], in3=Op[3], in4=not_12_out, out=open
  not not_12 (not_12_out, Op[4]);
  // AND_Gate and_8 has open pins: in0=Op[0], in1=Op[1], in2=Op[2], in3=Op[3], in4=not_13_out, out=open
  not not_13 (not_13_out, Op[4]);
  and and_9 (and_9_out, Zero, EX_BEQ);
  not not_14 (not_14_out, Zero);
  and and_10 (and_10_out, not_14_out, EX_BNE);
  or or_3 (Kill2, and_9_out, and_10_out);
  and and_11 (J, Jump, not_15_out);
  not not_15 (not_15_out, Kill2);
  or or_4 (Kill1, Kill2, J);
  Priority_Encoder #(.select(2)) priority_encoder_1 (
    .in0(1'b1), .in1(Kill2), .in2(J), .out(out_8));  // open: in3, gs, en_out, en_in

  // Other names for the same wires on the sheet: BEQ = EX_BEQ; BNE = EX_BNE; Br = Kill2; ZeroFlag = Zero
endmodule

module HazardCtrl (
  input  [2:0] Rs,
  input  [2:0] Rd4Out,
  input  WBRegWr,
  input  [2:0] Rd3Out,
  input  MEMRegWr,
  input  [2:0] Rd2Out,
  input  EXRegWr,
  input  EXMemRd,
  input  [2:0] Rt,
  output [1:0] FwA,
  output Stall,
  output [1:0] FwB
);

  wire and_1_out, and_2_out, and_3_out, and_4_out, and_5_out, and_6_out, comparator_1_eq, comparator_2_eq,
       comparator_3_eq, comparator_4_eq, comparator_5_eq, comparator_6_eq, comparator_7_eq, comparator_8_eq,
       comparator_9_eq, comparator_10_eq, comparator_11_eq, comparator_12_eq, comparator_13_eq,
       comparator_14_eq, comparator_15_eq, not_1_out, not_2_out, not_3_out, not_4_out, not_5_out, not_6_out,
       or_1_out;

  Comparator #(.mode("unsigned"), .width(3)) comparator_1 (.a(Rs), .b(3'b000), .eq(comparator_1_eq));  // open: gt, lt
  Comparator #(.mode("unsigned"), .width(3)) comparator_2 (.a(Rs), .b(Rd4Out), .eq(comparator_2_eq));  // open: gt, lt
  Comparator #(.mode("unsigned"), .width(3)) comparator_3 (.a(Rs), .b(3'b000), .eq(comparator_3_eq));  // open: gt, lt
  Comparator #(.mode("unsigned"), .width(3)) comparator_4 (.a(Rs), .b(Rd3Out), .eq(comparator_4_eq));  // open: gt, lt
  Comparator #(.mode("unsigned"), .width(3)) comparator_5 (.a(Rs), .b(3'b000), .eq(comparator_5_eq));  // open: gt, lt
  Comparator #(.mode("unsigned"), .width(3)) comparator_6 (.a(Rs), .b(Rd2Out), .eq(comparator_6_eq));  // open: gt, lt
  Comparator #(.mode("unsigned"), .width(3)) comparator_7 (.a(Rt), .b(3'b000), .eq(comparator_7_eq));  // open: gt, lt
  Comparator #(.mode("unsigned"), .width(3)) comparator_8 (.a(Rt), .b(Rd4Out), .eq(comparator_8_eq));  // open: gt, lt
  Comparator #(.mode("unsigned"), .width(3)) comparator_9 (.a(Rt), .b(3'b000), .eq(comparator_9_eq));  // open: gt, lt
  Comparator #(.mode("unsigned"), .width(3)) comparator_10 (.a(Rt), .b(Rd3Out), .eq(comparator_10_eq));  // open: gt, lt
  Comparator #(.mode("unsigned"), .width(3)) comparator_11 (.a(Rt), .b(3'b000), .eq(comparator_11_eq));  // open: gt, lt
  Comparator #(.mode("unsigned"), .width(3)) comparator_12 (.a(Rt), .b(Rd2Out), .eq(comparator_12_eq));  // open: gt, lt
  not not_1 (not_1_out, comparator_1_eq);
  and and_1 (and_1_out, not_1_out, comparator_2_eq, WBRegWr);
  not not_2 (not_2_out, comparator_3_eq);
  and and_2 (and_2_out, not_2_out, comparator_4_eq, MEMRegWr);
  not not_3 (not_3_out, comparator_5_eq);
  and and_3 (and_3_out, not_3_out, comparator_6_eq, EXRegWr);
  not not_4 (not_4_out, comparator_7_eq);
  and and_4 (and_4_out, not_4_out, comparator_8_eq, WBRegWr);
  not not_5 (not_5_out, comparator_9_eq);
  and and_5 (and_5_out, not_5_out, comparator_10_eq, MEMRegWr);
  not not_6 (not_6_out, comparator_11_eq);
  and and_6 (and_6_out, not_6_out, comparator_12_eq, EXRegWr);
  Priority_Encoder #(.select(2)) priority_encoder_1 (
    .in0(1'b1), .in1(and_1_out), .in2(and_2_out), .in3(and_3_out), .out(FwA));  // open: gs, en_out, en_in
  Priority_Encoder #(.select(2)) priority_encoder_2 (
    .in0(1'b1), .in1(and_4_out), .in2(and_5_out), .in3(and_6_out), .out(FwB));  // open: gs, en_out, en_in
  Comparator #(.mode("unsigned"), .width(1)) comparator_13 (
    .a(EXMemRd), .b(1'b1), .eq(comparator_13_eq));  // open: gt, lt
  Comparator #(.mode("unsigned"), .width(2)) comparator_14 (.a(FwA), .b(2'b11), .eq(comparator_14_eq));  // open: gt, lt
  or or_1 (or_1_out, comparator_14_eq, comparator_15_eq);
  Comparator #(.mode("unsigned"), .width(2)) comparator_15 (.a(FwB), .b(2'b11), .eq(comparator_15_eq));  // open: gt, lt
  and and_7 (Stall, comparator_13_eq, or_1_out);
endmodule

module PcCtrl2 (
  input  [4:0] Op,
  input  Zero,
  input  [1:0] Func,
  input  Jump,
  input  EX_BEQ,
  input  EX_BNE,
  output [1:0] PCSrc,
  output Kill1,
  output Kill2
);

  wire and_1_out, and_2_out, J, Jr, not_1_out, not_2_out;

  and and_1 (and_1_out, Zero, EX_BEQ);
  not not_1 (not_1_out, Zero);
  and and_2 (and_2_out, not_1_out, EX_BNE);
  or or_1 (Kill2, and_1_out, and_2_out);
  and and_3 (J, Jump, not_2_out);
  not not_2 (not_2_out, Kill2);
  or or_2 (Kill1, Kill2, J);
  and and_4 (Jr, Op[0], Op[1], ~Op[2], ~Op[3], ~Op[4], Func[0], Func[1]);  // AND_Gate
  Priority_Encoder #(.select(2)) priority_encoder_1 (
    .in0(1'b1), .in1(J), .in2(Kill2), .in3(Jr), .out(PCSrc));  // open: gs, en_out, en_in

  // Other names for the same wires on the sheet: BEQ = EX_BEQ; BNE = EX_BNE; Br = Kill2; ZeroFlag = Zero
endmodule
